# Fritzing sketch iotFritzing (saved by Fritzing 0.9.10b)

parts:
  E1 = ESP32-Cam
  SP1 = SPEAKER [package=pcb_mount_speaker]  # not connected
  U1 = ESP32-38PinWide [part_number=ESP32-38PinWide]
  Part1 = adafruit [part_number="Adafruit #3006"]
  S1 = Pushbutton [package="[SMD]"]
  BAT1 = BC9VPC [package=bc9vpc]  # not connected
  USBTTL1 = USB A Plug
  USBTTL2 = Micro USB B Plug

nets:
  N1: E1.GPIO_13, U1.GPIO13, S1.Pin_3, S1.Pin_4
  N2: U1.GPIO25, Part1.connector20
  N3: U1.GPIO26, Part1.connector18
  N4: U1.GPIO27, Part1.connector19
  VIN: U1.GPIO11, U1.VIN, U1.GND, Part1.connector14, Part1.connector15, S1.Pin_1, S1.Pin_2, USBTTL1.usb, USBTTL2.usb

custom parts:
  ESP32-38PinWide: Generic 38-Pin ESP32 with wide format (only access to one side of pins on a breadboard) based on Stephen Lilley's HiLetgo ESP-WROOM-32 ESP32 ESP-32S Development Board.
